# Fritzing sketch Measurements_Proj (saved by Fritzing 0.9.9b)

parts:
  Mod1 = Raspberry Pi Pico W
  U1 = Turbidity Sensor Probe [package=THT]
  U2 = DFRobot SEN0189 [package=THT]

nets:
  N1: Mod1.pin_3, Mod1.pin_42, U2.P1_3
  N2: Mod1.pin_26, U2.P1_1
  N3: Mod1.pin_40, U2.P1_2
  N4: U1.pin1, U2.P2_3
  N5: U1.pin2, U2.P2_1
  N6: U1.VCC, U2.P2_2

custom parts:
  Raspberry Pi Pico W: Raspberry Pi Pico W. Based around the RP2040 microcontroller the Pico W is a low cost microcontroller device bringing Raspberry Pi quality, cost, and easy of use to the microcontroller space. The areas marked KEEPOUT in pcb silkscreen should not have traces running through them to avoid shorts on a soldered in module!
  Turbidity Sensor Probe: Turbidity sensor probe to the DFRobot measure module.
  DFRobot SEN0189: Turbidity sensor of DFRobot SEN0189
